# Fritzing sketch wireless switch protoboard (saved by Fritzing 0.9.3b)
perfboards: 1

parts:
  J1 = female pin header, 5 pins [form="♀ (female)"]
  J2 = female pin header, 6 pins [form="♀ (female)"]
  J4 = female pin header, 12 pins [form="♀ (female)"]
  J5 = female pin header, 12 pins [form="♀ (female)"]
  J3 = female pin header, 6 pins [form="♀ (female)"]

nets:
  N1: J1.pin1, J4.pin3
  N2: J1.pin5, J2.pin6, J5.pin1
  N3: J2.pin2, J5.pin3
  N4: J2.pin3, J4.pin5
  N5: J2.pin4, J4.pin6
  N6: J2.pin5, J5.pin5
  N7: J4.pin7, J3.pin4
